// Digital circuit ALU 1 Bit.dig as structural Verilog
module ALU_1_Bit (
  input  A,
  input  EN_A,
  input  B,
  input  EN_B,
  input  INV_A,
  input  CI,
  input  F_0,
  input  F_1,
  output O,
  output CO
);

  wire add_1_s, and_1_out, and_2_out, and_3_out, not_1_out, or_1_out, xor_1_out;

  and and_1 (and_1_out, A, EN_A);
  and and_2 (and_2_out, B, EN_B);
  xor xor_1 (xor_1_out, INV_A, and_1_out);
  and and_3 (and_3_out, xor_1_out, and_2_out);
  or or_1 (or_1_out, xor_1_out, and_2_out);
  not not_1 (not_1_out, and_2_out);
  Add add_1 (.a(xor_1_out), .b(and_2_out), .c_i(CI), .s(add_1_s), .c_o(CO));
  Multiplexer #(.Selector_Bits(2)) multiplexer_1 (
    .sel({F_0, F_1}), .in_0(and_3_out), .in_1(or_1_out), .in_2(not_1_out), .in_3(add_1_s), .out(O));
endmodule
