// Digital circuit ALU 16 Bit.dig as structural Verilog
module ALU_16_Bit (
  input  [15:0] A,
  input  EN_A,
  input  [15:0] B,
  input  EN_B,
  input  INV_A,
  input  CI,
  input  F_0,
  input  F_1,
  output [15:0] O,
  output CO
);

  wire alu_8_bit_1_co;

  ALU_8_Bit alu_8_bit_1 (
    .A(A[7:0]), .EN_A(EN_A), .B(B[7:0]), .EN_B(EN_B), .INV_A(INV_A), .CI(CI), .F_0(F_0), .F_1(F_1),
    .O(O[7:0]), .CO(alu_8_bit_1_co));
  ALU_8_Bit alu_8_bit_2 (
    .A(A[15:8]), .EN_A(EN_A), .B(B[15:8]), .EN_B(EN_B), .INV_A(INV_A), .CI(alu_8_bit_1_co), .F_0(F_0),
    .F_1(F_1), .O(O[15:8]), .CO(CO));
endmodule
