// Digital circuit ALU 32 Bit.dig as structural Verilog
module ALU_32_Bit (
  input  F_0,
  input  F_1,
  input  CI,
  input  INV_A,
  input  EN_B,
  input  EN_A,
  input  [31:0] B,
  input  [31:0] A,
  output [31:0] O,
  output CO,
  output Z,
  output N
);

  wire alu_16_bit_1_co;

  ALU_16_Bit alu_16_bit_1 (
    .A(A[15:0]), .EN_A(EN_A), .B(B[15:0]), .EN_B(EN_B), .INV_A(INV_A), .CI(CI), .F_0(F_0), .F_1(F_1),
    .O(O[15:0]), .CO(alu_16_bit_1_co));
  ALU_16_Bit alu_16_bit_2 (
    .A(A[31:16]), .EN_A(EN_A), .B(B[31:16]), .EN_B(EN_B), .INV_A(INV_A), .CI(alu_16_bit_1_co), .F_0(F_0),
    .F_1(F_1), .O({N, O[30:16]}), .CO(CO));
  Comparator #(.Bits(32)) comparator_1 (.a({N, O[30:0]}), .b({32{1'b0}}), .eq(Z));  // open: gt, lt

  assign O[31] = N;
endmodule
