// Digital circuit ALU 4 Bit.dig as structural Verilog
module ALU_4_Bit (
  input  [3:0] A,
  input  EN_A,
  input  [3:0] B,
  input  EN_B,
  input  INV_A,
  input  CI,
  input  F_0,
  input  F_1,
  output [3:0] O,
  output CO
);

  wire alu_1_bit_1_co, alu_1_bit_2_co, alu_1_bit_3_co;

  ALU_1_Bit alu_1_bit_1 (
    .A(A[0]), .EN_A(EN_A), .B(B[0]), .EN_B(EN_B), .INV_A(INV_A), .CI(CI), .F_0(F_0), .F_1(F_1), .O(O[0]),
    .CO(alu_1_bit_1_co));
  ALU_1_Bit alu_1_bit_2 (
    .A(A[1]), .EN_A(EN_A), .B(B[1]), .EN_B(EN_B), .INV_A(INV_A), .CI(alu_1_bit_1_co), .F_0(F_0), .F_1(F_1),
    .O(O[1]), .CO(alu_1_bit_2_co));
  ALU_1_Bit alu_1_bit_3 (
    .A(A[2]), .EN_A(EN_A), .B(B[2]), .EN_B(EN_B), .INV_A(INV_A), .CI(alu_1_bit_2_co), .F_0(F_0), .F_1(F_1),
    .O(O[2]), .CO(alu_1_bit_3_co));
  ALU_1_Bit alu_1_bit_4 (
    .A(A[3]), .EN_A(EN_A), .B(B[3]), .EN_B(EN_B), .INV_A(INV_A), .CI(alu_1_bit_3_co), .F_0(F_0), .F_1(F_1),
    .O(O[3]), .CO(CO));
endmodule
