// Digital circuit ALU 8 Bit.dig as structural Verilog
module ALU_8_Bit (
  input  [7:0] A,
  input  EN_A,
  input  [7:0] B,
  input  EN_B,
  input  INV_A,
  input  CI,
  input  F_0,
  input  F_1,
  output [7:0] O,
  output CO
);

  wire alu_4_bit_1_co;

  ALU_4_Bit alu_4_bit_1 (
    .A(A[3:0]), .EN_A(EN_A), .B(B[3:0]), .EN_B(EN_B), .INV_A(INV_A), .CI(CI), .F_0(F_0), .F_1(F_1),
    .O(O[3:0]), .CO(alu_4_bit_1_co));
  ALU_4_Bit alu_4_bit_2 (
    .A(A[7:4]), .EN_A(EN_A), .B(B[7:4]), .EN_B(EN_B), .INV_A(INV_A), .CI(alu_4_bit_1_co), .F_0(F_0),
    .F_1(F_1), .O(O[7:4]), .CO(CO));
endmodule
