// Digital circuit Mic1 Computer.dig as structural Verilog
module Mic1_Computer (
  input  clk,
  input  [8:0] in_4,
  output [8:0] out_2,
  output [35:0] out_3
);

  wire alu_32_bit_1_n, alu_32_bit_1_z, comparator_1_eq, comparator_2_eq, decoder_1_out_0, decoder_1_out_1,
       decoder_1_out_2, decoder_1_out_3, decoder_1_out_4, decoder_1_out_5, decoder_1_out_6, decoder_1_out_7,
       delay_1_out, delay_2_out;
  wire [7:0] bitextender_1_out, MBR_q, ramdualport_1_d;
  wire [23:0] MAR_q;
  wire [31:0] alu_32_bit_1_o, barrelshifter_1_out, barrelshifter_2_out, CPP_q, H_q, LV_q, MDR_q, OPC_q,
       or_1_out, PC_q, selector_1_o, SP_q, TOS_q;
  wire [31:8] ramdualport_1_d_2;
  wire [31:24] MAR_q_2;

  Delay #(.delayTime(2)) delay_1 (.in(clk), .out(delay_1_out));
  Delay delay_2 (.in(clk), .out(delay_2_out));
  RAMDualPort #(.AddrBits(24), .isProgramMemory("true"), .Bits(32)) ramdualport_1 (
    .A(MAR_q), .Din(MDR_q), .str(out_3[29]), .C(delay_1_out), .ld(out_3[30]),
    .D({ramdualport_1_d_2, ramdualport_1_d}));
  Register #(.Bits(32)) MAR (.D(or_1_out), .C(delay_2_out), .en(out_3[28]), .Q({MAR_q_2, MAR_q}));
  Register #(.Bits(32)) MDR (.D(or_1_out), .C(delay_2_out), .en(out_3[27]), .Q(MDR_q));
  Register #(.Bits(32)) PC (.D(or_1_out), .C(delay_2_out), .en(out_3[26]), .Q(PC_q));
  Register #(.Bits(8)) MBR (.D(ramdualport_1_d), .C(delay_2_out), .en(out_3[31]), .Q(MBR_q));
  Register #(.Bits(32)) SP (.D(or_1_out), .C(delay_2_out), .en(out_3[25]), .Q(SP_q));
  Register #(.Bits(32)) LV (.D(or_1_out), .C(delay_2_out), .en(out_3[24]), .Q(LV_q));
  Register #(.Bits(32)) CPP (.D(or_1_out), .C(delay_2_out), .en(out_3[23]), .Q(CPP_q));
  Register #(.Bits(32)) TOS (.D(or_1_out), .C(delay_2_out), .en(out_3[22]), .Q(TOS_q));
  Register #(.Bits(32)) OPC (.D(or_1_out), .C(delay_2_out), .en(out_3[21]), .Q(OPC_q));
  Register #(.Bits(32)) H (.D(or_1_out), .C(delay_2_out), .en(out_3[20]), .Q(H_q));
  Decoder #(.Selector_Bits(4)) decoder_1 (
    .sel(out_3[35:32]), .out_0(decoder_1_out_0), .out_1(decoder_1_out_1), .out_2(decoder_1_out_2),
    .out_3(decoder_1_out_3), .out_4(decoder_1_out_4), .out_5(decoder_1_out_5), .out_6(decoder_1_out_6),
    .out_7(decoder_1_out_7));  // open: out_8, out_9, out_10, out_11, out_12, out_13, out_14, out_15
  Selector selector_1 (.EN(decoder_1_out_7), .D(MDR_q), .O(selector_1_o));
  Selector selector_2 (.EN(decoder_1_out_6), .D(PC_q), .O(selector_1_o));
  Selector selector_3 (.EN(decoder_1_out_5), .D({{24{1'b0}}, MBR_q}), .O(selector_1_o));
  Selector selector_4 (.EN(decoder_1_out_4), .D(SP_q), .O(selector_1_o));
  Selector selector_5 (.EN(decoder_1_out_3), .D(LV_q), .O(selector_1_o));
  Selector selector_6 (.EN(decoder_1_out_2), .D(CPP_q), .O(selector_1_o));
  Selector selector_7 (.EN(decoder_1_out_1), .D(TOS_q), .O(selector_1_o));
  Selector selector_8 (.EN(decoder_1_out_0), .D(OPC_q), .O(selector_1_o));
  BitExtender #(.inputBits(1), .outputBits(8)) bitextender_1 (.in(out_3[11]), .out(bitextender_1_out));
  ALU_32_Bit alu_32_bit_1 (
    .F_0(out_3[14]), .F_1(out_3[15]), .CI(out_3[16]), .INV_A(out_3[17]), .EN_B(out_3[18]), .EN_A(out_3[19]),
    .B(selector_1_o), .A(H_q), .O(alu_32_bit_1_o), .Z(alu_32_bit_1_z), .N(alu_32_bit_1_n));  // open: CO
  BarrelShifter #(.Bits(32)) barrelshifter_1 (
    .in(alu_32_bit_1_o), .shift({{5{1'b0}}, out_3[13]}), .out(barrelshifter_1_out));
  assign or_1_out = barrelshifter_2_out | barrelshifter_1_out;  // Or or_1, 32 bits wide
  // And and_1 has open pins: In_1=MBR_q, In_2=bitextender_1_out, out=open
  Comparator comparator_1 (.a(out_3[10]), .b(alu_32_bit_1_z), .eq(comparator_1_eq));  // open: gt, lt
  BarrelShifter #(.Bits(32), .direction("right")) barrelshifter_2 (
    .in(alu_32_bit_1_o), .shift({{5{1'b0}}, out_3[12]}), .out(barrelshifter_2_out));
  Register #(.Bits(9), .isProgramCounter("true")) register_1 (.D(out_3[8:0]), .C(clk), .en(1'b1), .Q(out_2));
  // Or or_2 has open pins: In_1=comparator_1_eq, In_2=comparator_2_eq, out=open
  Comparator comparator_2 (.a(out_3[9]), .b(alu_32_bit_1_n), .eq(comparator_2_eq));  // open: gt, lt
  ROM #(.AddrBits(9), .Bits(36), .isProgramMemory("true")) Control_Store (.A(out_2), .sel(1'b1), .D(out_3));

  // Notes on the sheet:
  //   clk: Hz: 50
  //   contents of Control_Store (hex, n*v repeats v):
  //   1,2,3,4,5,6,7,8
endmodule
