// Digital circuit Selector.dig as structural Verilog
module Selector (
  input  EN,
  input  [31:0] D,
  output [31:0] O
);

  wire [31:0] bitextender_1_out;

  BitExtender #(.inputBits(1), .outputBits(32)) bitextender_1 (.in(EN), .out(bitextender_1_out));
  assign O = bitextender_1_out & D;  // And and_1, 32 bits wide
endmodule
